# Fritzing sketch MOD_1_power-supply (saved by Fritzing 0.7.1b)
breadboards: 1

parts:
  Part1 = Arduino Pro Mini 3.3V
  U1 = Voltage Regulator - 5V [package="TO220 [THT]"]
  U2 = Voltage Regulator - 3.3V [package="TO220 [THT]"]
  J1 = male pin header, 2 pins [form="♂ (male)"]
  D1 = Rectifier Diode [part_number=1N4001 package="300 mil [THT]"]
  J3 = female pin header, 2 pins [form="♀ (female)"]
  D3 = Rectifier Diode [part_number=1N4001 package="300 mil [THT]"]
  C1 = Electrolytic Capacitor [capacitance=1µF package="100 mil [THT, electrolytic]"]
  C2 = Electrolytic Capacitor [capacitance=1µF package="100 mil [THT, electrolytic]"]
  C3 = Electrolytic Capacitor [capacitance=1µF package="100 mil [THT, electrolytic]"]
  C4 = Electrolytic Capacitor [capacitance=1µF package="100 mil [THT, electrolytic]"]
  J2 = female pin header, 2 pins [form="♀ (female)"]

nets:
  N1: Part1.RAW, U1.output_voltage, C3.+
  GND: Part1.GND, U1.GND, U2.input_voltage, J1.pin2, J3.pin1, C1.-, C2.-, C3.-, C4.-, J2.pin1
  N2: U1.input_voltage, D1.cathode, C2.+
  N3: U2.GND, C4.+, J2.pin2
  N4: U2.output_voltage, D3.cathode, C1.+
  N5: J1.pin1, D1.anode
  N6: J3.pin2, D3.anode
